// Digital circuit register_file.dig as structural Verilog
module register_file (
  input  [1:0] Select_read1,
  input  [1:0] Select_read2,
  input  clk,
  input  [3:0] Write_data,
  input  [1:0] Select_write,
  input  [7:0] ctrl_registers,
  output [3:0] Read_data_1,
  output [3:0] Read_data_2
);

  wire [3:0] demultiplexer_1_out_0, demultiplexer_1_out_1, demultiplexer_1_out_2, demultiplexer_1_out_3,
       gpr_1_p4, gpr_2_p4, gpr_3_p4, gpr_4_p4;

  Demultiplexer #(.Selector_Bits(2), .Bits(4)) demultiplexer_1 (
    .sel(Select_write), .in(Write_data), .out_0(demultiplexer_1_out_0), .out_1(demultiplexer_1_out_1),
    .out_2(demultiplexer_1_out_2), .out_3(demultiplexer_1_out_3));
  // GPR gpr_1: pin names not known; wires that end beside it: clk, demultiplexer_1_out_0, ctrl_registers[1:0], gpr_1_p4
  // GPR gpr_2: pin names not known; wires that end beside it: clk, demultiplexer_1_out_1, ctrl_registers[3:2], gpr_2_p4
  // GPR gpr_3: pin names not known; wires that end beside it: clk, demultiplexer_1_out_2, ctrl_registers[5:4], gpr_3_p4
  // GPR gpr_4: pin names not known; wires that end beside it: clk, demultiplexer_1_out_3, ctrl_registers[7:6], gpr_4_p4
  Multiplexer #(.Selector_Bits(2), .Bits(4)) multiplexer_1 (
    .sel(Select_read1), .in_0(gpr_1_p4), .in_1(gpr_2_p4), .in_2(gpr_3_p4), .in_3(gpr_4_p4), .out(Read_data_1));
  Multiplexer #(.Selector_Bits(2), .Bits(4)) multiplexer_2 (
    .sel(Select_read2), .in_0(gpr_1_p4), .in_1(gpr_2_p4), .in_2(gpr_3_p4), .in_3(gpr_4_p4), .out(Read_data_2));
endmodule
